# Fritzing sketch AutomaticWatering (saved by Fritzing 0.9.3b)
circuit board: 8.46667cm x 5.64444cm
breadboards: 1

parts:
  Arduino_UNO = Arduino Uno (Rev3) - ICSP
  Hygrometer_Probe = FC-28 Soil Hygrometer Module - Probe
  Hygrometer_Sensor = FC-28 Soil Hygrometer Module
  Q2 = Basic FET N-Channel [package="TO220 [THT]"]
  VCC3 = Battery block 9V
  VCC4 = Battery block 9V
  Water_Pump = DC Motor
  R1 = Resistor [tolerance=±5% resistance=560 package=THT]
  Water_Level_Sensor = SWITCH-MOMENTARY-2 [package=reed_switch_pth]
  R2 = Resistor [tolerance=±5% resistance=10k package=THT]
  J1 = Piezo Speaker

nets:
  N1: Arduino_UNO.A0, Hygrometer_Sensor.AO
  GND: Arduino_UNO.GND, Hygrometer_Sensor.GND, Q2.source, Water_Pump.pin_1, R2.Pin_1, J1.pin1
  N2: Arduino_UNO.D2, R1.Pin_0
  N3: Arduino_UNO.D3_PWM, Water_Level_Sensor.2, R2.Pin_0
  N4: Arduino_UNO.D4, J1.pin2
  5V: Arduino_UNO.5V, Hygrometer_Sensor.VCC, Water_Level_Sensor.1
  N5: Hygrometer_Probe.POS, Hygrometer_Sensor.NEG
  N6: Hygrometer_Probe.NEG, Hygrometer_Sensor.POS
  N7: Q2.gate, R1.Pin_1
  N8: Q2.drain, VCC3.+
  N9: VCC3.-, VCC4.+
  N10: VCC4.-, Water_Pump.pin_2

custom parts:
  FC-28 Soil Hygrometer Module - Probe: The FC-28 is a soil hygrometer module that uses the Texas Instruments LM393 comparator chip to provide an analog measurement of soil humidity.
  FC-28 Soil Hygrometer Module: The FC-28 is a soil hygrometer module that uses the Texas Instruments LM393 comparator chip to provide an analog measurement of soil humidity. The digital output is high when soil moisture is over a certain threshold, as determined by adjusting the potentiometer.
